# Fritzing sketch Goodwatch_v2_2_order (saved by Fritzing 0.9.9b)
circuit board: 9.22033cm x 7.82544cm
breadboards: 1

parts:
  DSCPI-02_eINK_Connector = DESPI-C02
  FPC_Adatper_Light = FPC Adapter [package=THT]
  Q1 = Basic FET P-Channel [package="TO220 [THT]"]
  D32_Pro = Wemos Lolin D32 PRO v2
  Sensor_Interface1 = Sensor Interface [form="♂ (shrouded male)" package=THT]
  R1 = Resistor [tolerance=±5% power=0.25 resistance=10k package=THT]
  R2 = Resistor [tolerance=±5% power=0.25 resistance=10k package=THT]
  DSC3231_Clock = Adafruit DS3231 REVERSE [part_number="Adafruit #3013"]
  MAX98357A = Adafruit MAX98357A I2S 3W Class D Amplifier [part_number="Adafruit #3006"]
  eInkPower = HW-045 2V-24V Einstellbar Boost Modul 2A [form="♀ (female)" package=THT]

nets:
  VIN: DSCPI-02_eINK_Connector.3V, D32_Pro.3V, Sensor_Interface1.VIN, R1.Pin_0, DSC3231_Clock.VIN
  GND: DSCPI-02_eINK_Connector.GND, D32_Pro.GND, Sensor_Interface1.GND, R2.Pin_1, DSC3231_Clock.GND, MAX98357A.GND, eInkPower.VIN_GND
  N1: DSCPI-02_eINK_Connector.SDI, D32_Pro.23
  N2: DSCPI-02_eINK_Connector.SCK, D32_Pro.18
  N3: DSCPI-02_eINK_Connector.CS, D32_Pro.5
  N4: DSCPI-02_eINK_Connector.DC, D32_Pro.0
  N5: DSCPI-02_eINK_Connector.RES, D32_Pro.2
  N6: DSCPI-02_eINK_Connector.Busy, D32_Pro.15
  N7: FPC_Adatper_Light.Pin_2, FPC_Adatper_Light.pin1, eInkPower.VOUT+
  N8: FPC_Adatper_Light.pin6, FPC_Adatper_Light.pin5, Q1.drain
  N9: Q1.gate, D32_Pro.27
  N10: Q1.source, eInkPower.VOUT_GND
  N11: D32_Pro.VN, R1.Pin_1, DSC3231_Clock.SQW
  N12: D32_Pro.34, Sensor_Interface1.IRD_IRQ
  N13: D32_Pro.32, Sensor_Interface1.I2S_DIN
  N14: D32_Pro.33, Sensor_Interface1.I2S_LRC
  N15: D32_Pro.25, Sensor_Interface1.I2S_BCLK
  N16: D32_Pro.26, MAX98357A.DIN
  N17: D32_Pro.14, MAX98357A.LRCLK
  N18: D32_Pro.12, MAX98357A.BCLK
  N19: D32_Pro.13, R2.Pin_0, eInkPower.SLEEP_MODE
  N20: D32_Pro.BAT, MAX98357A.VIN, eInkPower.VIN+
  N21: D32_Pro.21, Sensor_Interface1.I2C_SDA, DSC3231_Clock.SDA
  N22: D32_Pro.22, Sensor_Interface1.I2C_SCL, DSC3231_Clock.SCL

notes:
  GND
  VIN
  IRD - I2S BCLK
  I2C SCL-I2S LRC
  I2C SDA-I2S DIN
  Vout-
  Vout+
  S
  D
  G
  3V
  VBAT
  DS3231
  MAX98357A
  GW 2.2

custom parts:
  FPC Adapter: FPC Adapter for GoodWatch Power Supply
  Wemos Lolin D32 PRO v2: Wemos Lolin 32 wifi and blue tooth board based on the ESP-32 cpu, digital I/Os 26, analog inputs 12, clock 240mhz, Flash 4Mbytes, lipo battery charger (500ma connection broken out on breadboard but not pcb), usb. The mounting holes are only set on the silkscreen, if you want actual holes in the pcb copy the hole from the pcb menu in parts over the top of the hole in the silkscreen.
  Adafruit DS3231 REVERSE: The datasheet for the DS3231 explains that this part is an "Extremely Accurate I²C-Integrated RTC/TCXO/Crystal". And, hey, it does exactly what it says on the tin! This Real Time Clock (RTC) is the most precise you can get in a small, low power package. Most RTCs use an external 32kHz timing crystal that is used to keep time with low current draw. And that's all well and good, but those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
  Adafruit MAX98357A I2S 3W Class D Amplifier: Listen to this good news - we now have an all in one digital audio amp breakout board that works incredibly well with the Raspberry Pi! If you're looking for an easy and low cost way to get you digital sound files bumpin' then the MAX08357 I2S Amp Breakout is for you. It takes standard I2S digital audio input and, not only decodes it into analog, but also amplifies it directly into a speaker.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
  HW-045 2V-24V Einstellbar Boost Modul 2A: Generic female header
